# Fritzing sketch DoorActuator (saved by Fritzing 0.9.3b)
breadboards: 1

parts:
  Part1 = Photon
  DRV_1 = DRV 8825 Stepper Motor Carrier, High Current [part_number="DRV 8825"]
  C1 = Capacitor Polarized [package=cpol-radial-100uf-25v]
  S1 = SPST Switch [package=switch-spdt-smd]
  S2 = SPST Switch [package=switch-spdt-smd]
  M1 = Stepper Motor - Bipolar  # not connected
  VCC1 = 4 x AAA Battery Mount
  SONAR1 = Maxbotix MaxSonar Ultrasonic Sensor (Hi-Res)
  R1 = Resistor [tolerance=±5% resistance=220 package="0402 [SMD]"]
  S3 = Momentary Switch [package=ksa_sealed_tac_switch]
  LED2 = LED - 5mm [color="Red (633nm)" package="5 mm [THT]"]
  U1 = Voltage Regulator - 5V [package="TO220 [THT]"]  # not connected

nets:
  N1: Part1.A2, SONAR1.AN
  N2: Part1.D3, DRV_1.SLEEP
  N3: Part1.D4, S1.O
  N4: Part1.D5, S2.P
  N5: Part1.D6, S3.3
  N6: Part1.D7, LED2.cathode
  3V3: Part1.3V3, SONAR1.+5V, S3.1
  N7: C1.+, VCC1.-
  N8: C1.-, VCC1.+
  N9: S1.P, S2.O, R1.Pin_1
  N10: SONAR1.GND, LED2.anode

custom parts:
  Maxbotix MaxSonar Ultrasonic Sensor (Hi-Res): Maxbotix MaxSonar Hi-Resolution Ultrasonic Sensor HRLV-EZ0, HRLV-EZ1, HRLV-EZ2, HRLV-EZ3, HRLV-EZ4
